# Fritzing sketch schematic (saved by Fritzing 1.0.0rc)
breadboards: 1

parts:
  LCD1 = LCD screen
  LCM1602_IIC1 = LCM1602 IIC [part_number="LCM1602 IIC" chip_label="LCM1602 IIC" package="DIP (Dual Inline) [THT]"]
  Componente1 = Arduino Uno (Rev3)
  RHT1 = Humidity and Temperature Sensor RHT03
  R1 = Resistor [tolerance=±5% resistance=4700 package="2010 [SMD]"]
  KY-1 = Keyes Relay [package=THT]
  Componente2 = FC-28 Soil Hygrometer Module
  Componente3 = FC-28 Soil Hygrometer Module - Probe
  Keypad4x1 = Keypad Membran 4x4

nets:
  VSS: LCD1.VSS, LCM1602_IIC1.VSS
  VDD: LCD1.VDD, LCM1602_IIC1.VDD
  N1: LCD1.V0, LCM1602_IIC1.V0
  N2: LCD1.RS, LCM1602_IIC1.RS
  N3: LCD1.R/W, LCM1602_IIC1.RW
  N4: LCD1.E, LCM1602_IIC1.E
  N5: LCD1.DB0, LCM1602_IIC1.D0
  N6: LCD1.DB1, LCM1602_IIC1.D1
  N7: LCD1.DB2, LCM1602_IIC1.D2
  N8: LCD1.DB3, LCM1602_IIC1.D3
  N9: LCD1.DB4, LCM1602_IIC1.D4
  N10: LCD1.DB5, LCM1602_IIC1.D5
  N11: LCD1.DB6, LCM1602_IIC1.D6
  N12: LCD1.DB7, LCM1602_IIC1.D7
  N13: LCD1.LED+, LCM1602_IIC1.A
  N14: LCD1.LED-, LCM1602_IIC1.K
  GND: LCM1602_IIC1.GND, Componente1.GND, RHT1.GND_2, KY-1.ground, Componente2.GND
  VCC: LCM1602_IIC1.VCC, Componente1.5V, RHT1.Vcc, R1.Pin_0, KY-1.power, Componente2.VCC
  N15: LCM1602_IIC1.SDA, Componente1.A4/SDA
  N16: LCM1602_IIC1.SCL, Componente1.A5/SCL
  N17: LCM1602_IIC1.LED_A, LCM1602_IIC1.LED_B
  N18: Componente1.A1, Componente2.AO
  N19: Componente1.D8, Keypad4x1.Pin4
  N20: Componente1.D9_PWM, Keypad4x1.Pin3
  N21: Componente1.D10_PWM/SS, Keypad4x1.Pin2
  N22: Componente1.D11_PWM/MOSI, Keypad4x1.Pin1
  N23: Componente1.D2, RHT1.Data-signal, R1.Pin_1
  N24: Componente1.D3_PWM, KY-1.signal
  N25: Componente1.D4, Keypad4x1.Pin8
  N26: Componente1.D5_PWM, Keypad4x1.Pin7
  N27: Componente1.D6_PWM, Keypad4x1.Pin6
  N28: Componente1.D7, Keypad4x1.Pin5
  N29: Componente2.POS, Componente3.NEG
  N30: Componente2.NEG, Componente3.POS

custom parts:
  LCM1602 IIC: I2C-Module to use a 1602 or 2004 LCD on with the wire.h libory Serial LCD Modul
  Keyes Relay: The Keyes 5V relay module is suitable for SCM development, home appliance control. It uses a 5V~12V TIL control signal which can control DC / AC signal.
  FC-28 Soil Hygrometer Module: The FC-28 is a soil hygrometer module that uses the Texas Instruments LM393 comparator chip to provide an analog measurement of soil humidity. The digital output is high when soil moisture is over a certain threshold, as determined by adjusting the potentiometer.
  FC-28 Soil Hygrometer Module - Probe: The FC-28 is a soil hygrometer module that uses the Texas Instruments LM393 comparator chip to provide an analog measurement of soil humidity.
  Keypad Membran 4x4: Membrane Keypad 4x4 Matrix
